# Fritzing sketch booster (saved by Fritzing 0.9.3b)
breadboards: 1

parts:
  R1 = Resistor [tolerance=±5% resistance=1M package="1206 [SMD]"]
  Q1 = TRANSISTOR_NPN [package=to-92-ammo]
  Pot_100k = POT [package=pot_alpha_rv16af-20]
  C3 = Electrolytic Capacitor [capacitance=100µF package="200 mil [THT, electrolytic]"]
  R2 = Resistor [tolerance=±5% resistance=10k package="1206 [SMD]"]
  R3 = Resistor [tolerance=±5% resistance=100k package="1206 [SMD]"]
  C1 = Electrolytic Capacitor [capacitance=100μF voltage=10V package="0807 [SMD, electrolytic]"]
  Output = Audio Jack (TRS) 3.5mm [package="PG203J [THT]"]
  Input = Audio Jack (TRS) 3.5mm [package="4Ucon 08780 [THT]"]
  VCC1 = Battery block 9V
  R4 = Resistor [tolerance=±5% resistance=560 package="0402 [SMD]"]
  C2 = Electrolytic Capacitor [capacitance=0.1µF package="200 mil [THT, electrolytic]"]

nets:
  N1: R1.Pin_0, Q1.B, R3.Pin_1, C1.-
  N2: R1.Pin_1, C3.+, R2.Pin_0, VCC1.+
  N3: Q1.E, R4.Pin_0
  N4: Q1.C, R2.Pin_1, C2.-
  N5: Pot_100k.A, C3.-, R3.Pin_0, Output.Ring, Output.Tip, Input.Ring, Input.Tip, VCC1.-, R4.Pin_1
  N6: C1.+, Input.Sleeve
